# Fritzing sketch stuart_v2 (saved by Fritzing 0.8.7b)
circuit board: 3.83422cm x 4.99945cm
breadboards: 1
stripboards: 1

parts:
  Arduino = Arduino Nano (Rev3.0)
  M1 = DC Motor
  M2 = DC Motor
  IC1 = FRM050 [package=THT]
  IC2 = FRM050 [package=THT]
  J2 = Screw terminal - 2 pins [package=THT]
  J3 = Screw terminal - 2 pins [package=THT]
  VCC1 = 4 x AAA Battery Mount
  J5 = Screw terminal - 2 pins [package=THT]
  J4 = Screw terminal - 2 pins [package=THT]

nets:
  N1: Arduino.GND, IC1.In_6, IC2.In_6, VCC1.-, J5.pin1
  N2: Arduino.D3, IC1.In_4
  N3: Arduino.D5, IC1.+V
  N4: Arduino.D6, IC2.In_4
  N5: Arduino.D9, J4.pin1
  N6: Arduino.D11/MOSI, IC2.+V
  N7: Arduino.VIN, VCC1.+, J5.pin2
  N8: Arduino.5V, J4.pin2
  N9: Arduino.3V3, IC1.Out_4, IC2.Out_4
  N10: M1.pin_1, IC1.0V, J3.pin1
  N11: M1.pin_2, IC1.Out_6, J3.pin2
  N12: M2.pin_1, IC2.0V, J2.pin1
  N13: M2.pin_2, IC2.Out_6, J2.pin2

notes:
  ant
  gnd
  vcc
  data

custom parts:
  4 x AAA Battery Mount: A 4 x AAA battery pack (4.8 Volts with recharables)
